# Fritzing sketch L-Star (saved by Fritzing 0.9.1b)
circuit board: 15.5861cm x 10.7994cm
breadboards: 1

parts:
  Propeller1 = Parallax Propeller D40 [package="DIP [THT]"]
  65C02 = WDC 65C02S [chip_label="WDC 65C02" package="DIP (Dual Inline) [THT]"]
  IC2 = 24LC256 [package=THT]
  RESET_PROP = Pushbutton [package="[THT]"]
  RESET_65C02 = Pushbutton [package="[THT]"]
  R1 = Resistor [tolerance=±5% resistance=3.3k package=THT]
  R2 = Resistor [tolerance=±5% resistance=3.3k package=THT]
  5MHz = CRYSTAL [package=hc49us]
  PS/2_Keyboard = mini DIN 6 Connector [package=mini-din6]
  Video_out = RCA [package=rca_lock]
  R3 = Resistor [tolerance=±5% resistance=220 package=THT]
  Power_in = Power Jack [package=power_jack_pth_lock]
  R4 = Resistor [tolerance=±5% resistance=100 package=THT]
  R5 = Resistor [tolerance=±5% resistance=100 package=THT]
  R6 = Resistor [tolerance=±5% resistance=10k package=THT]
  R7 = Resistor [tolerance=±5% resistance=10k package=THT]
  R8 = Resistor [tolerance=±5% resistance=10k package=THT]
  Prop_Plug = Header 4 [package=molex-1x4_lock]
  5V = Voltage Regulator - 5V [package="TO220 [THT]"]
  3V3 = Voltage Regulator - 3.3V [package="TO220 [THT]"]

nets:
  N1: Propeller1.P0, 65C02.D0
  N2: Propeller1.P1, 65C02.D1
  N3: Propeller1.P2, 65C02.D2
  N4: Propeller1.P3, 65C02.D3
  N5: Propeller1.P4, 65C02.D4
  N6: Propeller1.P5, 65C02.D5
  N7: Propeller1.P6, 65C02.D6
  N8: Propeller1.P7, 65C02.D7
  GND: Propeller1.VSS, Propeller1.BOEn, 65C02.VSS, IC2.A0, IC2.A1, IC2.A2, IC2.0V, IC2.WP_-_Write_Protect, RESET_PROP.Pin_1, RESET_PROP.Pin_2, RESET_65C02.Pin_3, RESET_65C02.Pin_4, PS/2_Keyboard.3, Video_out.SHELL, Power_in.GND, 5V.GND, 3V3.GND
  N9: Propeller1.RESn, RESET_PROP.Pin_3, RESET_PROP.Pin_4, Prop_Plug.2
  VDD: Propeller1.VDD, 65C02.VDD, IC2.+V, R1.Pin_0, R2.Pin_1, R6.Pin_1, R7.Pin_1, R8.Pin_0, 3V3.output_voltage
  N10: Propeller1.P8, 65C02.A0
  N11: Propeller1.P9, 65C02.A1
  N12: Propeller1.P10, 65C02.A2
  N13: Propeller1.P11, 65C02.A3
  N14: Propeller1.P12, 65C02.A4
  N15: Propeller1.P13, 65C02.A5
  N16: Propeller1.P14, 65C02.A6
  N17: Propeller1.P15, 65C02.A7
  N18: Propeller1.P16, 65C02.A8
  N19: Propeller1.P17, 65C02.A9
  N20: Propeller1.P18, 65C02.A10
  N21: Propeller1.P19, 65C02.A11
  N22: Propeller1.P20, 65C02.A12
  N23: Propeller1.P21, 65C02.A13
  N24: Propeller1.P22, 65C02.A14
  N25: Propeller1.P23, 65C02.A15
  N26: Propeller1.XI, 5MHz.2
  N27: Propeller1.XO, 5MHz.1
  N28: Propeller1.P24, 65C02.RWB
  N29: Propeller1.P25, R3.Pin_1
  N30: Propeller1.P26, R4.Pin_1
  N31: Propeller1.P27, R5.Pin_1
  N32: Propeller1.P28, 65C02.PHI2, IC2.SCL_-_I2C_Clock
  N33: Propeller1.P29, IC2.SDA_-_I2C_Data, R8.Pin_1, Prop_Plug.1
  N34: Propeller1.P30, Prop_Plug.4
  N35: Propeller1.P31, Prop_Plug.3
  N36: 65C02.RDY, 65C02.IRQB, 65C02.NMIB, 65C02.BE, 65C02.SOB, R2.Pin_0
  N37: 65C02.RESB, RESET_65C02.Pin_1, RESET_65C02.Pin_2, R1.Pin_1
  N38: PS/2_Keyboard.1, R4.Pin_0, R6.Pin_0
  N39: PS/2_Keyboard.4, 5V.output_voltage, 3V3.input_voltage
  N40: PS/2_Keyboard.5, R5.Pin_0, R7.Pin_0
  N41: Video_out.PIN, R3.Pin_0
  N42: Power_in.PWR, 5V.input_voltage

custom parts:
  WDC 65C02S: The Western Design Center version of the 65C02
